# Fritzing sketch YADioderHack (saved by Fritzing 0.9.2b)
circuit board: 8.46667cm x 5.64444cm
breadboards: 1

parts:
  STRIP1 = Header 4 [package=1x04-smd]
  STRIP2 = Header 4 [package=1x04-smd]
  PWR = Header 2 [package=jst-2-pth-kit]
  ATMEGA328 = atmega328 [package=dip]  # not connected
  Q1 = NPN-Transistor [package="TO92 [THT]"]
  Q2 = NPN-Transistor [package="TO92 [THT]"]
  Q3 = NPN-Transistor [package="TO92 [THT]"]
  Q4 = NPN-Transistor [package="TO92 [THT]"]
  Q5 = NPN-Transistor [package="TO92 [THT]"]
  Q6 = NPN-Transistor [package="TO92 [THT]"]
  STRIP4 = Header 4 [package=1x04-smd]
  STRIP3 = Header 4 [package=1x04-smd]

nets:
  N1: STRIP1.Red, STRIP2.Red, Q3.C
  N2: STRIP1.Blue, STRIP2.Blue, Q2.C
  N3: STRIP1.Green, STRIP2.Green, Q1.C
  +12V: STRIP1.+12V, STRIP2.+12V, PWR.2, STRIP4.+12V, STRIP3.+12V
  N4: PWR.1, Q1.E, Q2.E, Q3.E, Q4.E, Q5.E, Q6.E
  N5: Q4.C, STRIP4.Blue, STRIP3.Blue
  N6: Q5.C, STRIP4.Green, STRIP3.Green
  N7: Q6.C, STRIP4.Red, STRIP3.Red

custom parts:
  Header 4: Header 4 Standard 4-pin 0.1 header. Use with straight break away headers (SKU : PRT-00116), right angle break away headers (PRT-00553), swiss pins (PRT-00743), machine pins (PRT-00117), and female headers (PRT-00115). Molex polarized connector foot print use with SKU : PRT-08231 with associated crimp pins and housings. 1MM SMD Version SKU: PRT-10208
